# Fritzing sketch button_keyboard (saved by Fritzing 0.9.3b)
breadboards: 2

parts:
  Part1 = Arduino Uno (Rev3)
  R1 = Resistor [tolerance=±5% resistance=220 package=THT]
  S6 = Pushbutton [package="[THT]"]
  S5 = Pushbutton [package="[THT]"]
  S4 = Pushbutton [package="[THT]"]
  S2 = Pushbutton [package="[THT]"]
  S3 = Pushbutton [package="[THT]"]
  R2 = Resistor [tolerance=±5% resistance=220 package=THT]
  R3 = Resistor [tolerance=±5% resistance=220 package=THT]
  R4 = Resistor [tolerance=±5% resistance=220 package=THT]
  R5 = Resistor [tolerance=±5% resistance=220 package=THT]
  SPKR1 = Loudspeaker

nets:
  N1: Part1.D8, SPKR1.pin2
  N2: Part1.D9_PWM, S5.Pin_3, S5.Pin_4, R5.Pin_1
  N3: Part1.D10_PWM/SS, S4.Pin_3, S4.Pin_4, R4.Pin_1
  N4: Part1.D11_PWM/MOSI, S2.Pin_3, S2.Pin_4, R3.Pin_0
  N5: Part1.D12/MISO, S3.Pin_3, S3.Pin_4, R2.Pin_0
  N6: Part1.D13/SCK, R1.Pin_0, S6.Pin_3, S6.Pin_4
  N7: Part1.5V, S6.Pin_1, S6.Pin_2, S5.Pin_1, S5.Pin_2, S4.Pin_1, S4.Pin_2, S3.Pin_1, S3.Pin_2
  N8: Part1.GND, R1.Pin_1, R2.Pin_1, R3.Pin_1, R4.Pin_0, R5.Pin_0, SPKR1.pin1
  N9: S2.Pin_1, S2.Pin_2
