# Fritzing sketch joystick (saved by Fritzing 0.9.3b)
breadboards: 2

parts:
  POT1 = Analog Thumb Joystick
  Part1 = Arduino Uno (Rev3)
  J1 = Basic Servo
  LD1 = LD

nets:
  GND: POT1.GND, Part1.GND, J1.gnd, LD1.cathode
  N1: POT1.Select, Part1.D8
  N2: POT1.Yout, Part1.A1
  N3: POT1.Xout, Part1.A0
  VCC: POT1.Vcc, Part1.5V, J1.vcc, LD1.anode
  N4: Part1.D5_PWM, J1.pulse

custom parts:
  LD: A Generic Red Dot Laser Diode Module (~5mW)
