# Fritzing sketch pot_instrument (saved by Fritzing 0.9.3b)
breadboards: 1

parts:
  Part1 = Arduino Uno (Rev3)
  R1 = Rotary Potentiometer (Small) [maximum_resistance=100kΩ package=THT]
  SPKR1 = Loudspeaker
  R2 = Resistor [tolerance=±5% resistance=220 package=THT]

nets:
  N1: Part1.A0, R1.wiper
  N2: Part1.D13/SCK, R2.Pin_0
  N3: Part1.5V, R1.leg2
  N4: Part1.GND, R1.leg1, SPKR1.pin1
  N5: SPKR1.pin2, R2.Pin_1
